// Logisim project CPU.circ as structural Verilog: 15 circuits, main circuit main
module main (
);

  CPU cpu_1 ();  // open: in_1, out_2
endmodule

module CPU (
  input  [15:0] in_1,
  output [7:0] out_2
);

  wire AC_INPUT_RAM, AC_OUTPUT_RAM, c3, c4, CLK, COMP, EE_RAM, M1_CTR8, M2, M3, nand_1_out, not_1_out,
       not_2_out, OP, PARAR, PRINT, R_AC, s_r_ff_1_q;
  wire [7:0] AC, counter_1_q, demultiplexer_1_out1, demultiplexer_1_out1_2, demultiplexer_3_out0,
       demultiplexer_3_out1, EE, EE_Conteudo, multiplexer_1_out, multiplexer_3_out, multiplexer_4_out, PC_q,
       ula_1_r;
  wire [15:0] demultiplexer_2_out0, IR, multiplexer_2_out, ram_1_dout;

  Counter counter_1 (
    .clr(PARAR), .load(M1_CTR8), .up(1'b1), .count(not_1_out), .clk(not_2_out), .D(EE), .Q(counter_1_q));  // open: carry
  not not_1 (not_1_out, EE_RAM);
  not not_2 (not_2_out, CLK);
  Clock clock_1 (.out(CLK));
  Register PC (.D(counter_1_q), .clk(CLK), .Q(PC_q), .clr(PARAR));  // open: en
  UC uc_1 (
    .IR(IR), .c3(c3), .c4(c4), .M2(M2), .M3(M3), .EE(EE), .R_AC(R_AC), .OP(OP),
    .AC_OUTPUT_RAM(AC_OUTPUT_RAM), .AC_INPUT_RAM(AC_INPUT_RAM), .PRINT(PRINT), .PARAR(PARAR), .COMP(COMP),
    .M1_CTR8(M1_CTR8), .EE_RAM(EE_RAM));
  RAM #(.dataWidth(16)) ram_1 (
    .addr(multiplexer_1_out), .we(M3), .oe(nand_1_out), .clk(CLK), .din(multiplexer_2_out), .dout(ram_1_dout));
  Multiplexer #(.width(8)) multiplexer_1 (.in0(PC_q), .in1(EE), .out(multiplexer_1_out), .sel(EE_RAM));
  nand nand_1 (nand_1_out, M2, CLK);
  Multiplexer #(.width(16)) multiplexer_2 (
    .in0(in_1), .in1({AC, {8{1'b0}}}), .out(multiplexer_2_out), .sel(AC_INPUT_RAM));
  Multiplexer #(.width(8)) multiplexer_3 (.in0(EE_Conteudo), .in1({8{1'b0}}), .out(multiplexer_3_out), .sel(COMP));
  Demultiplexer #(.width(16)) demultiplexer_1 (
    .out1({demultiplexer_1_out1_2, demultiplexer_1_out1}), .in(ram_1_dout), .sel(s_r_ff_1_q));  // open: out0
  S_R_Flip_Flop s_r_ff_1 (.Q(s_r_ff_1_q), .preset(CLK));  // open: S, R, clk, reset, Qn
  Demultiplexer #(.width(16)) demultiplexer_2 (
    .out0(demultiplexer_2_out0), .in({demultiplexer_1_out1_2, demultiplexer_1_out1}), .sel(EE_RAM));  // open: out1
  Register #(.width(16)) u_IR (.D(demultiplexer_2_out0), .clk(CLK), .Q(IR), .clr(PARAR));  // open: en
  Demultiplexer #(.width(8)) demultiplexer_3 (
    .out0(demultiplexer_3_out0), .out1(demultiplexer_3_out1), .in(demultiplexer_1_out1), .sel(AC_OUTPUT_RAM));
  ULA ula_1 (.A(AC), .B(multiplexer_3_out), .OP(OP), .R(ula_1_r), .c3(c3), .c4(c4));  // open: o1, o2, c0, c1, c2, c5
  Demultiplexer #(.width(8)) demultiplexer_4 (.out0(EE_Conteudo), .out1(out_2), .in(demultiplexer_3_out0), .sel(PRINT));
  Multiplexer #(.width(8)) multiplexer_4 (
    .in0(demultiplexer_3_out1), .in1(ula_1_r), .out(multiplexer_4_out), .sel(R_AC));
  Register u_AC (.D(multiplexer_4_out), .clk(CLK), .Q(AC), .clr(PARAR));  // open: en
endmodule

module UC (
  input  [15:0] IR,
  input  c3,
  input  c4,
  output M2,
  output M3,
  output [7:0] EE,
  output R_AC,
  output OP,
  output AC_OUTPUT_RAM,
  output AC_INPUT_RAM,
  output PRINT,
  output PARAR,
  output COMP,
  output M1_CTR8,
  output EE_RAM
);

  wire decoder_1_out1, decoder_1_out2, decoder_1_out3, decoder_1_out4, decoder_1_out7, decoder_1_out8,
       decoder_1_out10, decoder_1_out11, decoder_1_out14, decoder_1_out15, instrucao_1_1_ee_ram_1,
       instrucao_1_1_m2_1, instrucao_2_1_ee_ram_2, instrucao_2_1_m3_2, instrucao_7_1_ee_ram_7,
       instrucao_7_1_m3_7, instrucao_8_1_ee_ram_8, instrucao_8_1_m2_8, nor_1_out;

  nor nor_1 (nor_1_out, IR[12], IR[13], IR[14], IR[15]);
  Decoder #(.select(4)) decoder_1 (
    .out1(decoder_1_out1), .out2(decoder_1_out2), .out3(decoder_1_out3), .out4(decoder_1_out4),
    .out7(decoder_1_out7), .out8(decoder_1_out8), .out9(PARAR), .out10(decoder_1_out10),
    .out11(decoder_1_out11), .out14(decoder_1_out14), .out15(decoder_1_out15), .sel(IR[11:8]), .en(nor_1_out));  // open: out0, out5, out6, out12, out13
  Instrucao_1 instrucao_1_1 (
    .I1(decoder_1_out1), .M2_1(instrucao_1_1_m2_1), .EE_RAM_1(instrucao_1_1_ee_ram_1),
    .AC_OUTPUT_RAM_1(AC_OUTPUT_RAM));
  Instrucao_2 instrucao_2_1 (
    .I2(decoder_1_out2), .M3_2(instrucao_2_1_m3_2), .EE_RAM_2(instrucao_2_1_ee_ram_2),
    .AC_INPUT_RAM_2(AC_INPUT_RAM));
  Instrucao_3_e_4 instrucao_3_e_4_1 (.I3(decoder_1_out3), .I4(decoder_1_out4), .R_AC(R_AC), .OP(OP));
  Instrucao_7 instrucao_7_1 (.I7(decoder_1_out7), .EE_RAM_7(instrucao_7_1_ee_ram_7), .M3_7(instrucao_7_1_m3_7));
  Instrucao_8 instrucao_8_1 (
    .I8(decoder_1_out8), .EE_RAM_8(instrucao_8_1_ee_ram_8), .M2_8(instrucao_8_1_m2_8), .PRINT(PRINT));
  Instrucao_A_ate_F instrucao_a_ate_f_1 (
    .IA(decoder_1_out10), .IB(decoder_1_out11), .ID(decoder_1_out14), .I_F(decoder_1_out15), .c3(c3),
    .c4(c4), .COMP(COMP), .M1_CTR8(M1_CTR8));
  or or_1 (EE_RAM, instrucao_8_1_ee_ram_8, instrucao_7_1_ee_ram_7, instrucao_2_1_ee_ram_2, instrucao_1_1_ee_ram_1);
  or or_2 (M2, instrucao_1_1_m2_1, instrucao_8_1_m2_8);
  or or_3 (M3, instrucao_2_1_m3_2, instrucao_7_1_m3_7);

  assign EE = IR[7:0];

  // Other names for the same wires on the sheet: INSTR[3:0] = IR[11:8]
endmodule

module ULA (
  input  [7:0] A,
  input  [7:0] B,
  input  OP,
  output [7:0] R,
  output o1,
  output o2,
  output c0,
  output c1,
  output c2,
  output c3,
  output c4,
  output c5
);

  OP_Aritmetico_8bit op_aritmetico_8bit_1 (.A(A), .B(B), .OP(OP), .R(R), .CS(o2), .SS(o1));
  Comp_8bit comp_8bit_1 (.A(A), .B(B), .c0(c0), .c1(c1), .c2(c2), .c3(c3), .c4(c4), .c5(c5));
endmodule

module Instrucao_1 (
  input  I1,
  output M2_1,
  output EE_RAM_1,
  output AC_OUTPUT_RAM_1
);


  assign AC_OUTPUT_RAM_1 = I1;
  assign EE_RAM_1 = I1;
  assign M2_1 = I1;
endmodule

module Instrucao_2 (
  input  I2,
  output M3_2,
  output EE_RAM_2,
  output AC_INPUT_RAM_2
);


  assign AC_INPUT_RAM_2 = I2;
  assign EE_RAM_2 = I2;
  assign M3_2 = I2;
endmodule

module Instrucao_3_e_4 (
  input  I3,
  input  I4,
  output R_AC,
  output OP
);

  or or_1 (R_AC, I3, I4);

  assign OP = I4;
endmodule

module Instrucao_7 (
  input  I7,
  output EE_RAM_7,
  output M3_7
);


  assign EE_RAM_7 = I7;
  assign M3_7 = I7;
endmodule

module Instrucao_8 (
  input  I8,
  output EE_RAM_8,
  output M2_8,
  output PRINT
);


  assign EE_RAM_8 = I8;
  assign M2_8 = I8;
  assign PRINT = I8;
endmodule

module Instrucao_A_ate_F (
  input  IA,
  input  IB,
  input  ID,
  input  I_F,
  input  c3,
  input  c4,
  output COMP,
  output M1_CTR8
);

  wire and_1_out, and_2_out, and_3_out, nor_1_out;

  nor nor_1 (nor_1_out, c3, c4);
  and and_1 (and_1_out, IB, c4);
  and and_2 (and_2_out, ID, c3);
  and and_3 (and_3_out, I_F, nor_1_out);
  or or_1 (COMP, IA, IB, ID, I_F);
  or or_2 (M1_CTR8, IA, and_1_out, and_2_out, and_3_out);
endmodule

module OP_Aritmetico_8bit (
  input  [7:0] A,
  input  [7:0] B,
  input  OP,
  output [7:0] R,
  output CS,
  output SS
);

  wire somador_8bit_1_c_out_7, somador_8bit_1_c_out_8;

  Somador_8bit somador_8bit_1 (
    .A(A), .B(B), .c_in_0(OP), .R(R), .c_out_7(somador_8bit_1_c_out_7), .c_out_8(somador_8bit_1_c_out_8));
  xor xor_1 (CS, somador_8bit_1_c_out_7, somador_8bit_1_c_out_8);
  xor xor_2 (SS, somador_8bit_1_c_out_8, OP);
endmodule

module Somador_8bit (
  input  [7:0] A,
  input  [7:0] B,
  input  c_in_0,
  output [7:0] R,
  output c_out_7,
  output c_out_8
);

  wire somador_1bit_1_c_out, somador_1bit_2_c_out, somador_1bit_3_c_out, somador_1bit_4_c_out,
       somador_1bit_5_c_out, somador_1bit_6_c_out, xor_1_out, xor_2_out, xor_3_out, xor_4_out, xor_5_out,
       xor_6_out, xor_7_out, xor_8_out;

  xor xor_1 (xor_1_out, B[0], c_in_0);
  xor xor_2 (xor_2_out, B[1], c_in_0);
  xor xor_3 (xor_3_out, B[2], c_in_0);
  xor xor_4 (xor_4_out, B[3], c_in_0);
  xor xor_5 (xor_5_out, B[4], c_in_0);
  xor xor_6 (xor_6_out, B[5], c_in_0);
  xor xor_7 (xor_7_out, B[6], c_in_0);
  xor xor_8 (xor_8_out, B[7], c_in_0);
  Somador_1bit somador_1bit_1 (.a(A[0]), .b(xor_1_out), .c_in(c_in_0), .s(R[0]), .c_out(somador_1bit_1_c_out));
  Somador_1bit somador_1bit_2 (
    .a(A[1]), .b(xor_2_out), .c_in(somador_1bit_1_c_out), .s(R[1]), .c_out(somador_1bit_2_c_out));
  Somador_1bit somador_1bit_3 (
    .a(A[2]), .b(xor_3_out), .c_in(somador_1bit_2_c_out), .s(R[2]), .c_out(somador_1bit_3_c_out));
  Somador_1bit somador_1bit_4 (
    .a(A[3]), .b(xor_4_out), .c_in(somador_1bit_3_c_out), .s(R[3]), .c_out(somador_1bit_4_c_out));
  Somador_1bit somador_1bit_5 (
    .a(A[4]), .b(xor_5_out), .c_in(somador_1bit_4_c_out), .s(R[4]), .c_out(somador_1bit_5_c_out));
  Somador_1bit somador_1bit_6 (
    .a(A[5]), .b(xor_6_out), .c_in(somador_1bit_5_c_out), .s(R[5]), .c_out(somador_1bit_6_c_out));
  Somador_1bit somador_1bit_7 (.a(A[6]), .b(xor_7_out), .c_in(somador_1bit_6_c_out), .s(R[6]), .c_out(c_out_7));
  Somador_1bit somador_1bit_8 (.a(A[7]), .b(xor_8_out), .c_in(c_out_7), .s(R[7]), .c_out(c_out_8));
endmodule

module Somador_1bit (
  input  a,
  input  b,
  input  c_in,
  output s,
  output c_out
);

  wire and_1_out, and_2_out, xor_1_out;

  xor xor_1 (xor_1_out, a, b);
  xor xor_2 (s, xor_1_out, c_in);
  and and_1 (and_1_out, c_in, xor_1_out);
  and and_2 (and_2_out, a, b);
  or or_1 (c_out, and_1_out, and_2_out);
endmodule

module Comp_8bit (
  input  [7:0] A,
  input  [7:0] B,
  output c0,
  output c1,
  output c2,
  output c3,
  output c4,
  output c5
);

  wire and_1_out, and_2_out, and_3_out, and_4_out, and_5_out, and_6_out, and_7_out, comp_1bit_1_a_maior,
       comp_1bit_1_iguais, comp_1bit_2_a_maior, comp_1bit_2_iguais, comp_1bit_3_a_maior, comp_1bit_3_iguais,
       comp_1bit_4_a_maior, comp_1bit_4_iguais, comp_1bit_5_a_maior, comp_1bit_5_iguais, comp_1bit_6_a_maior,
       comp_1bit_6_iguais, comp_1bit_7_a_maior, comp_1bit_7_iguais, comp_1bit_8_a_maior, comp_1bit_8_b_maior,
       comp_1bit_8_iguais, or_1_out, or_2_out, or_3_out, or_4_out, or_5_out, or_6_out;

  Comp_1bit comp_1bit_1 (
    .a(A[0]), .b(B[0]), .a_maior(comp_1bit_1_a_maior), .iguais(comp_1bit_1_iguais));  // open: b_maior
  Comp_1bit comp_1bit_2 (
    .a(A[1]), .b(B[1]), .a_maior(comp_1bit_2_a_maior), .iguais(comp_1bit_2_iguais));  // open: b_maior
  Comp_1bit comp_1bit_3 (
    .a(A[2]), .b(B[2]), .a_maior(comp_1bit_3_a_maior), .iguais(comp_1bit_3_iguais));  // open: b_maior
  Comp_1bit comp_1bit_4 (
    .a(A[3]), .b(B[3]), .a_maior(comp_1bit_4_a_maior), .iguais(comp_1bit_4_iguais));  // open: b_maior
  Comp_1bit comp_1bit_5 (
    .a(A[4]), .b(B[4]), .a_maior(comp_1bit_5_a_maior), .iguais(comp_1bit_5_iguais));  // open: b_maior
  Comp_1bit comp_1bit_6 (
    .a(A[5]), .b(B[5]), .a_maior(comp_1bit_6_a_maior), .iguais(comp_1bit_6_iguais));  // open: b_maior
  Comp_1bit comp_1bit_7 (
    .a(A[6]), .b(B[6]), .a_maior(comp_1bit_7_a_maior), .iguais(comp_1bit_7_iguais));  // open: b_maior
  Comp_1bit comp_1bit_8 (
    .a(A[7]), .b(B[7]), .a_maior(comp_1bit_8_a_maior), .iguais(comp_1bit_8_iguais),
    .b_maior(comp_1bit_8_b_maior));
  and and_1 (and_1_out, comp_1bit_1_a_maior, comp_1bit_2_iguais);
  or or_1 (or_1_out, and_1_out, comp_1bit_2_a_maior);
  and and_2 (and_2_out, or_1_out, comp_1bit_3_iguais);
  or or_2 (or_2_out, and_2_out, comp_1bit_3_a_maior);
  and and_3 (and_3_out, or_2_out, comp_1bit_4_iguais);
  or or_3 (or_3_out, and_3_out, comp_1bit_4_a_maior);
  and and_4 (and_4_out, or_3_out, comp_1bit_5_iguais);
  or or_4 (or_4_out, and_4_out, comp_1bit_5_a_maior);
  and and_5 (and_5_out, or_4_out, comp_1bit_6_iguais);
  or or_5 (or_5_out, and_5_out, comp_1bit_6_a_maior);
  and and_6 (and_6_out, or_5_out, comp_1bit_7_iguais);
  or or_6 (or_6_out, and_6_out, comp_1bit_7_a_maior);
  and and_7 (and_7_out, or_6_out, comp_1bit_8_iguais);
  or or_7 (c0, and_7_out, comp_1bit_8_a_maior);
  or or_8 (c4, comp_1bit_8_b_maior, and_7_out);
  and and_8 (c2, comp_1bit_1_iguais, comp_1bit_2_iguais, comp_1bit_3_iguais, comp_1bit_4_iguais, comp_1bit_5_iguais, comp_1bit_6_iguais, comp_1bit_7_iguais, comp_1bit_8_iguais);
  nor nor_1 (c3, A[0], A[1], A[2], A[3], A[4], A[5], A[6], A[7]);
  nor nor_2 (c1, c0, c2);
  nor nor_3 (c5, c4, c2);
endmodule

module Comp_1bit (
  input  a,
  input  b,
  output a_maior,
  output iguais,
  output b_maior
);

  wire xor_1_out;

  xor xor_1 (xor_1_out, a, b);
  not not_1 (iguais, xor_1_out);
  and and_1 (a_maior, a, xor_1_out);
  and and_2 (b_maior, xor_1_out, b);
endmodule
